// Logisim project bcd-7-segment-decoder.circ as structural Verilog: 1 circuit, main circuit BCD to 7-segment decoder
module BCD_to_7_segment_decoder (
  input  _0,
  input  _1,
  input  _2,
  input  _3,
  output A,
  output B,
  output C,
  output D,
  output E,
  output F,
  output G
);

  wire decoder_1_out0, decoder_1_out1, decoder_1_out2, decoder_1_out3, decoder_1_out4, decoder_1_out5,
       decoder_1_out6, decoder_1_out7, decoder_1_out9, decoder_1_out10, decoder_1_out11, decoder_1_out12,
       decoder_1_out13, decoder_1_out14, decoder_1_out15;

  Decoder #(.select(4), .tristate("false")) decoder_1 (
    .out0(decoder_1_out0), .out1(decoder_1_out1), .out2(decoder_1_out2), .out3(decoder_1_out3),
    .out4(decoder_1_out4), .out5(decoder_1_out5), .out6(decoder_1_out6), .out7(decoder_1_out7),
    .out9(decoder_1_out9), .out10(decoder_1_out10), .out11(decoder_1_out11), .out12(decoder_1_out12),
    .out13(decoder_1_out13), .out14(decoder_1_out14), .out15(decoder_1_out15), .sel({_3, _2, _1, _0}));  // open: out8
  nor nor_1 (A, decoder_1_out1, decoder_1_out4, decoder_1_out11, decoder_1_out13);
  nor nor_2 (B, decoder_1_out5, decoder_1_out6, decoder_1_out12, decoder_1_out14, decoder_1_out11, decoder_1_out15);
  nor nor_3 (C, decoder_1_out2, decoder_1_out12, decoder_1_out14, decoder_1_out15);
  nor nor_4 (D, decoder_1_out1, decoder_1_out4, decoder_1_out7, decoder_1_out10, decoder_1_out15);
  nor nor_5 (E, decoder_1_out1, decoder_1_out4, decoder_1_out5, decoder_1_out7, decoder_1_out9, decoder_1_out3);
  nor nor_6 (F, decoder_1_out1, decoder_1_out2, decoder_1_out3, decoder_1_out7, decoder_1_out13);
  nor nor_7 (G, decoder_1_out0, decoder_1_out1, decoder_1_out7, decoder_1_out12);
endmodule
