// Logisim project exp7-1b.circ as structural Verilog: 1 circuit, main circuit main
module main (
  input  [2:0] ABC,
  output F
);

  wire decoder_1_out1, decoder_1_out2, decoder_1_out6;

  Decoder #(.select(3), .tristate("false")) decoder_1 (
    .out1(decoder_1_out1), .out2(decoder_1_out2), .out6(decoder_1_out6), .sel(ABC));  // open: out0, out3, out4, out5, out7
  or or_1 (F, decoder_1_out1, decoder_1_out2, decoder_1_out6);

  // Notes on the sheet:
  //   Jenny Zhen
  //   CSCI-251-01
  //   Experiment 7-1A
endmodule
