// Logisim project exp7-1c.circ as structural Verilog: 1 circuit, main circuit main
module main (
  input  [2:0] ABC,
  output F
);

  Multiplexer #(.select(3), .width(1)) multiplexer_1 (
    .in0(1'b0), .in1(1'b1), .in2(1'b1), .in3(1'b0), .in4(1'b0), .in5(1'b0), .in6(1'b1), .in7(1'b0), .out(F),
    .sel(ABC));

  // Notes on the sheet:
  //   Jenny Zhen
  //   CSCI-251-01
  //   Experiment 7-1C
endmodule
