// Logisim project exp7-2b.circ as structural Verilog: 1 circuit, main circuit main
module main (
);

  wire and_1_out, and_2_out, bcd_to_7_segment_decoder_1_a, bcd_to_7_segment_decoder_1_b,
       bcd_to_7_segment_decoder_1_c, bcd_to_7_segment_decoder_1_d, bcd_to_7_segment_decoder_1_e,
       bcd_to_7_segment_decoder_1_f, bcd_to_7_segment_decoder_1_g, CLK_out, CLR_out, j_k_ff_1_q, j_k_ff_1_qn,
       j_k_ff_2_q, j_k_ff_2_qn, j_k_ff_3_q, j_k_ff_3_qn, j_k_ff_4_q;

  Button CLK (.out(CLK_out));
  J_K_Flip_Flop #(.trigger("rising")) j_k_ff_1 (
    .J(1'b1), .clk(CLK_out), .K(1'b1), .Q(j_k_ff_1_q), .Qn(j_k_ff_1_qn), .reset(CLR_out));  // open: preset, en
  Button CLR (.out(CLR_out));
  J_K_Flip_Flop #(.trigger("rising")) j_k_ff_2 (
    .J(j_k_ff_1_qn), .clk(CLK_out), .K(j_k_ff_1_qn), .Q(j_k_ff_2_q), .Qn(j_k_ff_2_qn), .reset(CLR_out));  // open: preset, en
  and and_1 (and_1_out, j_k_ff_1_qn, j_k_ff_2_qn);
  J_K_Flip_Flop #(.trigger("rising")) j_k_ff_3 (
    .J(and_1_out), .clk(CLK_out), .K(and_1_out), .Q(j_k_ff_3_q), .Qn(j_k_ff_3_qn), .reset(CLR_out));  // open: preset, en
  and and_2 (and_2_out, and_1_out, j_k_ff_3_qn);
  J_K_Flip_Flop #(.trigger("rising")) j_k_ff_4 (
    .J(and_2_out), .clk(CLK_out), .K(and_2_out), .Q(j_k_ff_4_q), .reset(CLR_out));  // open: Qn, preset, en
  BCD_to_7_segment_decoder bcd_to_7_segment_decoder_1 (
    ._0(j_k_ff_1_q), ._1(j_k_ff_2_q), ._2(j_k_ff_3_q), ._3(j_k_ff_4_q), .A(bcd_to_7_segment_decoder_1_a),
    .B(bcd_to_7_segment_decoder_1_b), .C(bcd_to_7_segment_decoder_1_c), .D(bcd_to_7_segment_decoder_1_d),
    .E(bcd_to_7_segment_decoder_1_e), .F(bcd_to_7_segment_decoder_1_f), .G(bcd_to_7_segment_decoder_1_g));
  _7_Segment_Display u_7_segment_display_1 (
    .g(bcd_to_7_segment_decoder_1_g), .f(bcd_to_7_segment_decoder_1_f), .a(bcd_to_7_segment_decoder_1_a),
    .b(bcd_to_7_segment_decoder_1_b), .e(bcd_to_7_segment_decoder_1_e), .d(bcd_to_7_segment_decoder_1_d),
    .c(bcd_to_7_segment_decoder_1_c));  // open: dp

  // Notes on the sheet:
  //   Jenny Zhen
  //   CSCI-251-01
  //   Experiment 7-2B
  //   J-K FlipFlops (left to right; lowest to highest order bit)
  //   First: Always flip the value every clock tick (period of 1), since a constant 11 is given.
  //   Second: Always flip the value every other clock tick (period of 2), since the negated output (to go in reverse) of the first J-K is given to both inputs. 
  //   Third: Always flip the value every 4 clock ticks (period of 4), since the negated outputs (to go in reverse) of the first two J-K are ANDed to be given to both inputs.
  //   Fourth: Always flip the value every 8 clock ticks (period of 8), since the negated outputs (to go in reverse) of the first three J-K are ANDed to be given to both inputs.
endmodule
