// Logisim project exp7-2c.circ as structural Verilog: 1 circuit, main circuit main
module main (
  input  Data
);

  wire bcd_to_7_segment_decoder_1_a, bcd_to_7_segment_decoder_1_b, bcd_to_7_segment_decoder_1_c,
       bcd_to_7_segment_decoder_1_d, bcd_to_7_segment_decoder_1_e, bcd_to_7_segment_decoder_1_f,
       bcd_to_7_segment_decoder_1_g, CLK_out, CLR_out, j_k_ff_1_q, j_k_ff_1_qn, j_k_ff_2_q, j_k_ff_2_qn,
       j_k_ff_3_q, j_k_ff_4_q, j_k_ff_4_qn, not_1_out;

  not not_1 (not_1_out, Data);
  Button CLK (.out(CLK_out));
  J_K_Flip_Flop #(.trigger("rising")) j_k_ff_1 (
    .J(Data), .clk(CLK_out), .K(not_1_out), .Q(j_k_ff_1_q), .Qn(j_k_ff_1_qn), .reset(CLR_out));  // open: preset, en
  Button CLR (.out(CLR_out));
  J_K_Flip_Flop #(.trigger("rising")) j_k_ff_2 (
    .J(j_k_ff_1_q), .clk(CLK_out), .K(j_k_ff_1_qn), .Q(j_k_ff_2_q), .Qn(j_k_ff_2_qn), .reset(CLR_out));  // open: preset, en
  J_K_Flip_Flop #(.trigger("rising")) j_k_ff_3 (
    .J(j_k_ff_4_q), .clk(CLK_out), .K(j_k_ff_4_qn), .Q(j_k_ff_3_q), .reset(CLR_out));  // open: Qn, preset, en
  J_K_Flip_Flop #(.trigger("rising")) j_k_ff_4 (
    .J(j_k_ff_2_q), .clk(CLK_out), .K(j_k_ff_2_qn), .Q(j_k_ff_4_q), .Qn(j_k_ff_4_qn), .reset(CLR_out));  // open: preset, en
  BCD_to_7_segment_decoder bcd_to_7_segment_decoder_1 (
    ._0(j_k_ff_3_q), ._1(j_k_ff_4_q), ._2(j_k_ff_2_q), ._3(j_k_ff_1_q), .A(bcd_to_7_segment_decoder_1_a),
    .B(bcd_to_7_segment_decoder_1_b), .C(bcd_to_7_segment_decoder_1_c), .D(bcd_to_7_segment_decoder_1_d),
    .E(bcd_to_7_segment_decoder_1_e), .F(bcd_to_7_segment_decoder_1_f), .G(bcd_to_7_segment_decoder_1_g));
  _7_Segment_Display u_7_segment_display_1 (
    .g(bcd_to_7_segment_decoder_1_g), .f(bcd_to_7_segment_decoder_1_f), .a(bcd_to_7_segment_decoder_1_a),
    .b(bcd_to_7_segment_decoder_1_b), .e(bcd_to_7_segment_decoder_1_e), .d(bcd_to_7_segment_decoder_1_d),
    .c(bcd_to_7_segment_decoder_1_c));  // open: dp

  // Notes on the sheet:
  //   Jenny Zhen
  //   CSCI-251-01
  //   Experiment 7-2C
  //   J-K FlipFlops (left to right; highest to lowest order bit)
  //   The inputs Q and !Q are given as inputs to pass along Q to the next J-K.
  //   Like a bubble, the bit is shifted/passed down the line.
endmodule
