// Logisim project exp8-1.circ as structural Verilog: 2 circuits, main circuit 1-bit ALU
module _1_bit_ALU (
  input  add_sub,
  input  C_in,
  input  [1:0] Selects,
  input  A,
  input  B,
  input  sli,
  output R,
  output C_out,
  output FA_out
);

  wire and_1_out, or_1_out, xor_1_out;

  and and_1 (and_1_out, A, B);
  or or_1 (or_1_out, A, B);
  xor xor_1 (xor_1_out, add_sub, B);
  Adder #(.width(1)) adder_1 (.a(A), .b(xor_1_out), .out(FA_out), .cin(C_in), .cout(C_out));
  Multiplexer #(.select(2), .width(1)) multiplexer_1 (
    .in0(and_1_out), .in1(or_1_out), .in2(FA_out), .in3(sli), .out(R), .sel(Selects));

  // Notes on the sheet:
  //   Name: Jenny
  //   Section #01
  //   Experiment #8
  //   Activity #1a
endmodule

module _4_bit_ALU (
  input  [3:0] A,
  input  [3:0] B,
  input  Add_Sub,
  input  [1:0] Select,
  output Zero,
  output [3:0] Result,
  output Overflow
);


  // Notes on the sheet:
  //   Name:
  //   Section #
  //   Experiment #
  //   Activity #
endmodule
